// Logisim project realALU.circ as structural Verilog: 7 circuits, main circuit main
module main (
  input  [3:0] aluOp,
  input  [7:0] inA,
  input  [7:0] inB,
  output [7:0] aluOut,
  output Z,
  output C,
  output N
);

  wire and_1_z__1_if_out____0x00, logicalshiftleft_1_c__1_if_out_8_____1,
       logicalshiftleft_1_n__1_if_out_7_____1, logicalshiftleft_1_z__1_if_out____0x00,
       logicalshiftright_1_c__1_if_out__1_____1, logicalshiftright_1_n__1_if_out_7_____1,
       logicalshiftright_1_z__1_if_out____0x00, not_1_out, not_2_z__1_if_out____0x00,
       or_1_z__1_if_out____0x00;
  wire [7:0] and_1_out, decoder8_1_output, decoder8_2_output, logicalshiftleft_1_out,
       logicalshiftright_1_out, not_2_out, or_1_out;

  decoder8 decoder8_1 (.Enable(not_1_out), .Select(aluOp[3:1]), .Output(decoder8_1_output));
  not not_1 (not_1_out, aluOp[0]);
  decoder8 decoder8_2 (.Enable(aluOp[0]), .Select(aluOp[3:1]), .Output(decoder8_2_output));
  AND and_1 (
    .inA(inA), .inB(inB), .out(and_1_out), .Enable(decoder8_1_output[0]),
    .Z__1_if_out____0x00(and_1_z__1_if_out____0x00));
  OR or_1 (
    .inA(inA), .inB(inB), .out(or_1_out), .Enable(decoder8_1_output[1]),
    .Z__1_if_out____0x00(or_1_z__1_if_out____0x00));
  NOT not_2 (.in(inB), .out(not_2_out), .Enable(decoder8_1_output[2]), .Z__1_if_out____0x00(not_2_z__1_if_out____0x00));
  logicalShiftRight logicalshiftright_1 (
    .in(inB), .out(logicalshiftright_1_out), .Enable(decoder8_1_output[3]),
    .Z__1_if_out____0x00(logicalshiftright_1_z__1_if_out____0x00),
    .C__1_if_out__1_____1(logicalshiftright_1_c__1_if_out__1_____1),
    .N__1_if_out_7_____1(logicalshiftright_1_n__1_if_out_7_____1));
  logicalShiftLeft logicalshiftleft_1 (
    .in(inB), .out(logicalshiftleft_1_out), .Enable(decoder8_1_output[4]),
    .C__1_if_out_8_____1(logicalshiftleft_1_c__1_if_out_8_____1),
    .N__1_if_out_7_____1(logicalshiftleft_1_n__1_if_out_7_____1),
    .Z__1_if_out____0x00(logicalshiftleft_1_z__1_if_out____0x00));
  or or_2 (C, logicalshiftright_1_c__1_if_out__1_____1, logicalshiftleft_1_c__1_if_out_8_____1);
  or or_3 (N, logicalshiftright_1_n__1_if_out_7_____1, logicalshiftleft_1_n__1_if_out_7_____1);
  assign aluOut = and_1_out | or_1_out | not_2_out | logicalshiftright_1_out | logicalshiftleft_1_out;  // OR_Gate or_4, 8 bits wide
  or or_5 (Z, and_1_z__1_if_out____0x00, or_1_z__1_if_out____0x00, not_2_z__1_if_out____0x00, logicalshiftright_1_z__1_if_out____0x00, logicalshiftleft_1_z__1_if_out____0x00);
endmodule

module AND (
  input  Enable,
  input  [7:0] inA,
  input  [7:0] inB,
  output [7:0] out,
  output Z__1_if_out____0x00
);

  wire nor_1_out;
  wire [7:0] and_1_out;

  assign and_1_out = inA & inB;  // AND_Gate and_1, 8 bits wide
  Transistor #(.\type ("n"), .width(8)) transistor_1 (.in(and_1_out), .out(out), .gate(Enable));
  Pull_Resistor pull_resistor_1 (.node(out));
  nor nor_1 (nor_1_out, and_1_out[0], and_1_out[1], and_1_out[2], and_1_out[3], and_1_out[4], and_1_out[5], and_1_out[6], and_1_out[7]);
  Pull_Resistor pull_resistor_2 (.node(Z__1_if_out____0x00));
  Transistor #(.\type ("n")) transistor_2 (.in(nor_1_out), .out(Z__1_if_out____0x00), .gate(Enable));
endmodule

module OR (
  input  Enable,
  input  [7:0] inA,
  input  [7:0] inB,
  output [7:0] out,
  output Z__1_if_out____0x00
);

  wire nor_1_out;
  wire [7:0] or_1_out;

  assign or_1_out = inA | inB;  // OR_Gate or_1, 8 bits wide
  Transistor #(.\type ("n"), .width(8)) transistor_1 (.in(or_1_out), .out(out), .gate(Enable));
  Pull_Resistor pull_resistor_1 (.node(out));
  nor nor_1 (nor_1_out, or_1_out[0], or_1_out[1], or_1_out[2], or_1_out[3], or_1_out[4], or_1_out[5], or_1_out[6], or_1_out[7]);
  Pull_Resistor pull_resistor_2 (.node(Z__1_if_out____0x00));
  Transistor #(.\type ("n")) transistor_2 (.in(nor_1_out), .out(Z__1_if_out____0x00), .gate(Enable));
endmodule

module NOT (
  input  Enable,
  input  [7:0] in,
  output [7:0] out,
  output Z__1_if_out____0x00
);

  wire nor_1_out;
  wire [7:0] not_1_out;

  assign not_1_out = ~in;  // NOT_Gate not_1, 8 bits wide
  Pull_Resistor pull_resistor_1 (.node(out));
  Transistor #(.\type ("n"), .width(8)) transistor_1 (.in(not_1_out), .out(out), .gate(Enable));
  nor nor_1 (nor_1_out, not_1_out[0], not_1_out[1], not_1_out[2], not_1_out[3], not_1_out[4], not_1_out[5], not_1_out[6], not_1_out[7]);
  Pull_Resistor pull_resistor_2 (.node(Z__1_if_out____0x00));
  Transistor #(.\type ("n")) transistor_2 (.in(nor_1_out), .out(Z__1_if_out____0x00), .gate(Enable));
endmodule

module logicalShiftRight (
  input  Enable,
  input  [7:0] in,
  output [7:0] out,
  output Z__1_if_out____0x00,
  output C__1_if_out__1_____1,
  output N__1_if_out_7_____1
);

  wire nor_1_out;

  Pull_Resistor pull_resistor_1 (.node(out));
  Transistor #(.\type ("n"), .width(8)) transistor_1 (.in({1'b0, in[7:1]}), .out(out), .gate(Enable));
  nor nor_1 (nor_1_out, in[1], in[2], in[3], in[4], in[5], in[6], in[7], 1'b0);
  Pull_Resistor pull_resistor_2 (.node(Z__1_if_out____0x00));
  Transistor #(.\type ("n")) transistor_2 (.in(nor_1_out), .out(Z__1_if_out____0x00), .gate(Enable));
  Pull_Resistor pull_resistor_3 (.node(C__1_if_out__1_____1));
  Transistor #(.\type ("n")) transistor_3 (.in(in[0]), .out(C__1_if_out__1_____1), .gate(Enable));
  Transistor #(.\type ("n")) transistor_4 (.in(1'b0), .out(N__1_if_out_7_____1), .gate(Enable));
  Pull_Resistor pull_resistor_4 (.node(N__1_if_out_7_____1));

  // Other names for the same wires on the sheet: C = in[0]
endmodule

module logicalShiftLeft (
  input  Enable,
  input  [7:0] in,
  output [7:0] out,
  output Z__1_if_out____0x00,
  output C__1_if_out_8_____1,
  output N__1_if_out_7_____1
);

  wire nor_1_out;

  Pull_Resistor pull_resistor_1 (.node(out));
  Transistor #(.\type ("n"), .width(8)) transistor_1 (.in({in[6:0], 1'b0}), .out(out), .gate(Enable));
  nor nor_1 (nor_1_out, 1'b0, in[0], in[1], in[2], in[3], in[4], in[5], in[6]);
  Pull_Resistor pull_resistor_2 (.node(Z__1_if_out____0x00));
  Transistor #(.\type ("n")) transistor_2 (.in(nor_1_out), .out(Z__1_if_out____0x00), .gate(Enable));
  Pull_Resistor pull_resistor_3 (.node(C__1_if_out_8_____1));
  Transistor #(.\type ("n")) transistor_3 (.in(in[7]), .out(C__1_if_out_8_____1), .gate(Enable));
  Transistor #(.\type ("n")) transistor_4 (.in(in[6]), .out(N__1_if_out_7_____1), .gate(Enable));
  Pull_Resistor pull_resistor_4 (.node(N__1_if_out_7_____1));

  // Other names for the same wires on the sheet: C = in[7]
endmodule

module decoder8 (
  input  Enable,
  input  [2:0] Select,
  output [7:0] Output
);

  wire [7:0] and_1_out;

  and and_1 (and_1_out[0], ~Select[0], ~Select[1], ~Select[2]);  // AND_Gate
  and and_2 (and_1_out[1], Select[0], ~Select[1], ~Select[2]);  // AND_Gate
  and and_3 (and_1_out[2], ~Select[0], Select[1], ~Select[2]);  // AND_Gate
  and and_4 (and_1_out[3], Select[0], Select[1], ~Select[2]);  // AND_Gate
  and and_5 (and_1_out[4], ~Select[0], ~Select[1], Select[2]);  // AND_Gate
  and and_6 (and_1_out[5], Select[0], ~Select[1], Select[2]);  // AND_Gate
  and and_7 (and_1_out[6], ~Select[0], Select[1], Select[2]);  // AND_Gate
  and and_8 (and_1_out[7], Select[0], Select[1], Select[2]);
  Pull_Resistor pull_resistor_1 (.node(Output));
  Transistor #(.\type ("n"), .width(8)) transistor_1 (.in(and_1_out), .out(Output), .gate(Enable));
endmodule
